# Fritzing sketch circuit (saved by Fritzing 0.9.6b)
breadboards: 1

parts:
  J1 = STM32 Nucleo boards
  J2 = Piezo Speaker
  J3 = Piezo Speaker
  R5 = Resistor [tolerance=±5% power=0.25 resistance=220 package=THT]
  R6 = Resistor [tolerance=±5% power=0.25 resistance=220 package=THT]
  R7 = Resistor [tolerance=±5% power=0.25 resistance=220 package=THT]
  R8 = Resistor [tolerance=±5% power=0.25 resistance=220 package=THT]
  R9 = Resistor [tolerance=±5% power=0.25 resistance=220 package=THT]
  RHT1 = Humidity and Temperature Sensor RHT03
  Componente1 = Gas Sensor Breakout Board
  LED1 = LED - 3mm [color="Red (633nm)" current=0.030 package="3 mm [THT]"]
  LED2 = LED - 3mm [color="Red (633nm)" current=0.030 package="3 mm [THT]"]
  LED3 = LED - 3mm [color="Red (633nm)" current=0.030 package="3 mm [THT]"]
  R10 = Resistor [tolerance=±5% power=0.25 resistance=220 package=THT]
  LED4 = LED - 3mm [color="Red (633nm)" current=0.030 package="3 mm [THT]"]
  LED5 = LED - 3mm [color="Red (633nm)" current=0.030 package="3 mm [THT]"]
  R11 = Resistor [tolerance=±5% power=0.25 resistance=220 package=THT]

nets:
  N1: J1.A0, Componente1.B1
  5V: J1.5V, RHT1.Vcc, Componente1.A1
  N2: J1.GND, R5.Pin_0, R6.Pin_0, R7.Pin_0, R8.Pin_0, R9.Pin_0, RHT1.GND_1, Componente1.B2, R10.Pin_0, R11.Pin_0
  N3: J2.pin1, R7.Pin_1
  N4: J3.pin1, R6.Pin_1
  N5: R5.Pin_1, LED1.cathode
  N6: R8.Pin_1, LED4.cathode
  N7: R9.Pin_1, LED2.cathode
  N8: Componente1.H1, Componente1.GND
  N9: LED3.cathode, R10.Pin_1
  N10: LED5.cathode, R11.Pin_1
