# Fritzing sketch individual-assign (saved by Fritzing 0.9.6b)
breadboards: 1

parts:
  J1 = STM32 Nucleo boards
  Componente1 = Gas Sensor Breakout Board
  RHT1 = Humidity and Temperature Sensor RHT03
  J2 = Piezo Speaker
  R1 = Resistor [tolerance=±5% resistance=220 package="2010 [SMD]"]
  J3 = Piezo Speaker
  R2 = Resistor [tolerance=±5% resistance=220 package="2010 [SMD]"]
  LED1 = smd LED [color="Red (633nm)" package="0805 [SMD]"]
  R3 = Resistor [tolerance=±5% resistance=220 package="2010 [SMD]"]
  LED2 = smd LED [color="Red (633nm)" package="0805 [SMD]"]
  R4 = Resistor [tolerance=±5% resistance=220 package="2010 [SMD]"]
  LED3 = smd LED [color="Red (633nm)" package="0805 [SMD]"]
  R5 = Resistor [tolerance=±5% resistance=220 package="2010 [SMD]"]
  LED4 = smd LED [color="Red (633nm)" package="0805 [SMD]"]
  LED5 = smd LED [color="Red (633nm)" package="0805 [SMD]"]
  R6 = Resistor [tolerance=±5% resistance=220 package="2010 [SMD]"]
  R7 = Resistor [tolerance=±5% resistance=220 package="2010 [SMD]"]

nets:
  GND: J1.GND, Componente1.GND, RHT1.GND_1, R1.Pin_0, R2.Pin_0
  N1: Componente1.H1, RHT1.Vcc
  N2: J2.pin1, R1.Pin_1
  N3: J3.pin1, R2.Pin_1
  N4: LED1.cathode, R3.Pin_1
  N5: R3.Pin_0, R4.Pin_0, R5.Pin_0, R6.Pin_0, R7.Pin_0
  N6: LED2.cathode, R4.Pin_1
  N7: LED3.cathode, R5.Pin_1
  N8: LED4.cathode, R7.Pin_1
  N9: LED5.cathode, R6.Pin_1
